# Fritzing sketch raspberry_pi_zero (saved by Fritzing 0.9.4)
perfboards: 1
breadboards: 1

parts:
  HEF1 = HEF4094 [package="DIP16 [THT]"]
  MCU1 = Raspberry Pi Zero
  U1 = RELAY-SOLIDSTATE [part_number=SSR package=relay-s108t02]
  U2 = RELAY-SOLIDSTATE [part_number=SSR package=relay-s108t02]
  U3 = RELAY-SOLIDSTATE [part_number=SSR package=relay-s108t02]
  U5 = RELAY-SOLIDSTATE [part_number=SSR package=relay-s108t02]
  U6 = RELAY-SOLIDSTATE [part_number=SSR package=relay-s108t02]
  U7 = RELAY-SOLIDSTATE [part_number=SSR package=relay-s108t02]
  U8 = RELAY-SOLIDSTATE [part_number=SSR package=relay-s108t02]
  U4 = RELAY-SOLIDSTATE [part_number=SSR package=relay-s108t02]
  R1 = Resistor [tolerance=±5% resistance=47k package=THT]
  R2 = Resistor [tolerance=±5% resistance=220 package=THT]
  R3 = Resistor [tolerance=±5% resistance=220 package=THT]
  R4 = Resistor [tolerance=±5% resistance=47k package=THT]

nets:
  N1: HEF1.STROBE, MCU1.pin_11, R1.Pin_0
  N2: HEF1.DATA, MCU1.pin_13, R2.Pin_0
  N3: HEF1.CLOCK, MCU1.pin_15, R3.Pin_0
  N4: HEF1.Q1, U1.+
  N5: HEF1.Q2, U2.+
  N6: HEF1.Q3, U3.+
  N7: HEF1.Q4, U4.+
  N8: HEF1.Vss, MCU1.pin_6, MCU1.pin_25, MCU1.pin_39, U1.-, U2.-, U3.-, U5.-, U6.-, U7.-, U8.-, U4.-, R1.Pin_1, R2.Pin_1, R3.Pin_1, R4.Pin_1
  N9: HEF1.Q8, U8.+
  N10: HEF1.Q7, U7.+
  N11: HEF1.Q6, U6.+
  N12: HEF1.Q5, U5.+
  N13: HEF1.OE, MCU1.pin_16, R4.Pin_0
  N14: HEF1.Vdd, MCU1.pin_2, MCU1.pin_4
